// Digital circuit MMP-1.dig as structural Verilog
module MMP_1 (
  input  in_1
);

  wire Addr_Dest, Addr_Src, Addr_Step, and_1_out, and_2_out, and_3_out, button_1_out, comparator_1_eq,
       comparator_1_gt, comparator_1_lt, decoder_1_out_3, or_1_out, Out_Dev;
  wire [1:0] counter_1_out;
  wire [15:0] Dest_q, driver_1_out, rom_1_d, Src_q, Step_out;
  wire [31:0] Temp_q;
  wire [31:16] rom_1_d_2;

  Button button_1 (.out(button_1_out));
  Register #(.Bits(16)) Src (.D(rom_1_d_2), .C(button_1_out), .en(Addr_Step), .Q(Src_q));
  Register #(.Bits(16)) Dest (.D(rom_1_d), .C(button_1_out), .en(Addr_Step), .Q(Dest_q));
  CounterPreset #(.Bits(16)) Step (
    .en(in_1), .C(button_1_out), .dir(1'b0), .in({16{1'b0}}), .ld(1'b0), .clr(1'b0), .out(Step_out));  // open: ovf
  // Probe on Src_q
  assign driver_1_out = Addr_Src ? Src_q : 16'bz;  // Driver driver_1
  // Probe on Dest_q
  assign driver_1_out = Addr_Dest ? Dest_q : 16'bz;  // Driver driver_2
  assign driver_1_out = Addr_Step ? Step_out : 16'bz;  // Driver driver_3
  // Probe on driver_1_out
  Comparator #(.Bits(16)) comparator_1 (
    .a(driver_1_out), .b(16'h4000), .gt(comparator_1_gt), .eq(comparator_1_eq), .lt(comparator_1_lt));
  and and_1 (and_1_out, comparator_1_lt, Out_Dev);
  and and_2 (and_2_out, Out_Dev, or_1_out);
  or or_1 (or_1_out, comparator_1_gt, comparator_1_eq);
  and and_3 (and_3_out, or_1_out, Addr_Dest);
  Counter #(.Bits(2)) counter_1 (.en(1'b1), .C(button_1_out), .clr(1'b0), .out(counter_1_out));  // open: ovf
  Decoder #(.Selector_Bits(2)) decoder_1 (
    .sel(counter_1_out), .out_0(Addr_Step), .out_1(Addr_Src), .out_2(Addr_Dest), .out_3(decoder_1_out_3));
  Register #(.Bits(32)) Temp (.D({rom_1_d_2, rom_1_d}), .C(button_1_out), .en(Addr_Src), .Q(Temp_q));
  // Probe on driver_1_out[13:0]
  ROM #(.bigEndian("true"), .AddrBits(14), .Bits(32)) rom_1 (
    .A(driver_1_out[13:0]), .sel(and_1_out), .D({rom_1_d_2, rom_1_d}));
  RAMSinglePortSel #(.AddrBits(14), .Bits(32)) ramsingleportsel_1 (
    .A(driver_1_out[13:0]), .CS(button_1_out), .WE(and_3_out), .OE(and_2_out), .D({rom_1_d_2, rom_1_d}));
  assign {rom_1_d_2, rom_1_d} = Addr_Dest ? Temp_q : 32'bz;  // Driver driver_4
  // Probe on {rom_1_d_2, rom_1_d}
  or or_2 (Out_Dev, Addr_Step, Addr_Src);

  // Other names for the same wires on the sheet: In_SrcDest = Addr_Step; In_Temp = Addr_Src; In_Dev = Addr_Dest;
  //   Out_Temp = Addr_Dest

  // Notes on the sheet:
  //   rom_1 loads program.bin
  //   Sequence:
  //   Addr: Step, Out: Dev, In: Src/Dest
  //   Addr: Src, Out: Dev, In: Temp
  //   Addr: Dest, Out: Temp, In: Dev
  //   If Dest != (address of Step) then increment Step
  //   0x0000-0x3FFF : ROM
  //   0x4000-0x7FFF : RAM
  //   0xF000-0xF001 : ALU operands
  //   0xF002-0xF00A : ALU SUM, AND, OR, XOR, NOT, GT, GTE, LT, LTE
  //   0xFFFF : Step
endmodule
